# Fritzing sketch pi-stopwatch (saved by Fritzing 0.9.3b)
stripboards: 1

parts:
  Raspberry_Pi_Zero1 = Raspberry Pi Zero
  OLED_I2C1 = OLED 128x64 I2C Monochrome Display
  Bauteil1 = Passive Buzzer
  Start = Momentary Switch [package=ksa_sealed_tac_switch]
  Reset = Momentary Switch [package=ksa_sealed_tac_switch]
  PIN_ENABLE = male pin header, 1 pin [form="♂ (male)"]
  PIN_END = male pin header, 1 pin [form="♂ (male)"]
  GND = male pin header, 1 pin [form="♂ (male)"]
  J1 = male pin header, 8 pins [form="♂ (male)"]

nets:
  3V3: Raspberry_Pi_Zero1.3v3, Raspberry_Pi_Zero1.3V3, OLED_I2C1.VDD, Bauteil1.S
  N1: Raspberry_Pi_Zero1.GPIO2, OLED_I2C1.SDA
  N2: Raspberry_Pi_Zero1.GPIO3, OLED_I2C1.SCK
  GND: Raspberry_Pi_Zero1.GND, OLED_I2C1.GND, Bauteil1.GND, Start.1, Start.2, Reset.3, Reset.4, GND.pin1, J1.pin3, J1.pin8
  N3: Raspberry_Pi_Zero1.GIPO5, Start.3, Start.4, J1.pin1
  N4: Raspberry_Pi_Zero1.GIPO6, Reset.1, Reset.2, J1.pin5
  N5: Raspberry_Pi_Zero1.GIPO13, PIN_ENABLE.pin1, J1.pin6
  N6: Raspberry_Pi_Zero1.GIPO19, PIN_END.pin1, J1.pin7
  N7: Raspberry_Pi_Zero1.GIPO24, Bauteil1.NC
